// Logisim project D-flip-flop.circ as structural Verilog: 1 circuit, main circuit main
module main (
  input  D,
  input  in_2,
  output out_3,
  output out_4,
  output out_5,
  output out_6
);

  wire clock_2_out, clock_out, nand_1_out, nand_2_out, nand_3_out;

  Clock clock (.out(clock_out));
  nand nand_1 (nand_1_out, in_2, in_2);
  Clock clock_2 (.out(clock_2_out));
  D_Flip_Flop d_ff_1 (.clk(clock_out), .D(D), .Q(out_3), .Qn(out_4));  // open: preset, en, reset
  nand nand_2 (nand_2_out, in_2, clock_2_out);
  nand nand_3 (nand_3_out, clock_2_out, nand_1_out);
  nand nand_4 (out_5, nand_2_out, out_6);
  nand nand_5 (out_6, out_5, nand_3_out);

  // Notes on the sheet:
  //   Dwij desai
  //   BDA08
  //   BAtch-14
endmodule
