// Logisim project J-Q_flip-flop.circ as structural Verilog: 1 circuit, main circuit main
module main (
  input  in_1,
  input  in_2,
  input  in_3,
  input  in_4,
  output out_5,
  output out_6,
  output out_7,
  output out_8
);

  wire clock_1_out, clock_2_out, nand_1_out, nand_2_out;

  Clock clock_1 (.out(clock_1_out));
  Clock clock_2 (.out(clock_2_out));
  J_K_Flip_Flop j_k_ff_1 (.J(in_1), .clk(clock_1_out), .K(in_2), .Q(out_5), .Qn(out_6));  // open: preset, en, reset
  nand nand_1 (nand_1_out, in_3, out_8, clock_2_out);
  nand nand_2 (nand_2_out, clock_2_out, out_7, in_4);
  nand nand_3 (out_7, nand_1_out, out_8);
  nand nand_4 (out_8, out_7, nand_2_out);

  // Notes on the sheet:
  //   Dwij desai
  //   BDA08
  //   Batch-14
endmodule
