// Logisim project S-Q.circ as structural Verilog: 1 circuit, main circuit main
module main (
  input  in_1,
  input  in_2,
  input  in_3,
  input  in_4,
  output out_5,
  output out_6,
  output out_7,
  output out_8
);

  wire clock_1_out, clock_2_out, nand_1_out, nand_2_out;

  Clock clock_1 (.out(clock_1_out));
  Clock clock_2 (.out(clock_2_out));
  nand nand_1 (nand_1_out, in_3, clock_2_out);
  nand nand_2 (nand_2_out, clock_2_out, in_4);
  S_R_Flip_Flop s_r_ff_1 (.S(in_1), .clk(clock_1_out), .R(in_2), .Q(out_5), .Qn(out_6));  // open: preset, reset, en
  nand nand_3 (out_7, nand_1_out, out_8);
  nand nand_4 (out_8, out_7, nand_2_out);

  // Notes on the sheet:
  //   Dwij desai
  //   BDA08
  //   BAtch-14
endmodule
