// Logisim project T-flip-flop.circ as structural Verilog: 1 circuit, main circuit main
module main (
  input  in_1,
  input  in_2,
  output out_3,
  output out_4,
  output out_5,
  output out_6
);

  wire clock_1_out, clock_2_out, nand_1_out, nand_2_out;

  Clock clock_1 (.out(clock_1_out));
  Clock clock_2 (.out(clock_2_out));
  T_Flip_Flop t_ff_1 (.clk(clock_1_out), .T(in_1), .Q(out_3), .Qn(out_4));  // open: preset, reset, en
  nand nand_1 (nand_1_out, in_2, out_6, clock_2_out);
  nand nand_2 (nand_2_out, clock_2_out, out_5, in_2);
  nand nand_3 (out_5, nand_1_out, out_6);
  nand nand_4 (out_6, out_5, nand_2_out);

  // Notes on the sheet:
  //   Dwij desai
  //   BDA08
  //   Batch-14
endmodule
