// Logisim project Practical_6.circ as structural Verilog: 1 circuit, main circuit main
module main (
  input  A,
  input  B,
  input  C,
  output Y0,
  output Y1,
  output Y2,
  output Y3,
  output Y4,
  output Y5,
  output Y6,
  output Y7
);

  wire A_prime_out, B_prime_out, C_prime_out;

  not A_prime (A_prime_out, A);
  not B_prime (B_prime_out, B);
  not C_prime (C_prime_out, C);
  and and_1 (Y0, A_prime_out, B_prime_out, C_prime_out);
  and and_2 (Y1, A_prime_out, B_prime_out, C);
  and and_3 (Y2, A_prime_out, B, C_prime_out);
  and and_4 (Y3, A_prime_out, B, C);
  and and_5 (Y4, A, B_prime_out, C_prime_out);
  and and_6 (Y5, A, B_prime_out, C);
  and and_7 (Y6, A, B, C_prime_out);
  and and_8 (Y7, A, B, C);
endmodule
