// Logisim project Magnitude Camparator.circ as structural Verilog: 1 circuit, main circuit main
module main (
  input  A,
  input  B,
  output A_B,
  output A_B_2,
  output A_B_3
);

  wire A_prime_out, B_prime_out;

  not A_prime (A_prime_out, A);
  not B_prime (B_prime_out, B);
  and and_1 (A_B, A_prime_out, B);
  xnor xnor_1 (A_B_2, A, B);
  and and_2 (A_B_3, A, B_prime_out);

  // Notes on the sheet:
  //   Dwij desai
  //   BDA08
  //   Batch-14
  //   Magnitude camparator
endmodule
