// Logisim project 1x4_Multiplexer.circ as structural Verilog: 1 circuit, main circuit main
module main (
  input  Din,
  input  S1,
  input  S0,
  output Y0,
  output Y1,
  output Y2,
  output Y3
);

  wire not_1_out, not_2_out;

  not not_1 (not_1_out, S1);
  not not_2 (not_2_out, S0);
  and and_1 (Y0, Din, not_1_out, not_2_out);
  and and_2 (Y1, Din, not_1_out, S0);
  and and_3 (Y2, Din, S1, not_2_out);
  and and_4 (Y3, Din, S1, S0);

  // Notes on the sheet:
  //   Dwij desai
  //   BDA08
  //   Batch-14
  //   1x4 de-Multiplexer
endmodule
