// Logisim project 4x1_Multiplexer.circ as structural Verilog: 1 circuit, main circuit main
module main (
  input  S1,
  input  S0,
  input  D0,
  input  D1,
  input  D2,
  input  D3,
  output Y
);

  wire and_1_out, and_2_out, and_3_out, and_4_out, not_1_out, not_2_out;

  not not_1 (not_1_out, S1);
  not not_2 (not_2_out, S0);
  and and_1 (and_1_out, D0, not_1_out, not_2_out);
  and and_2 (and_2_out, D1, not_1_out, S0);
  and and_3 (and_3_out, D2, S1, not_2_out);
  and and_4 (and_4_out, D3, S1, S0);
  or or_1 (Y, and_1_out, and_2_out, and_3_out, and_4_out);

  // Notes on the sheet:
  //   Dwij desai
  //   BDA08
  //   Batch-14
  //   4x1 Multiplexer
endmodule
