// Logisim project Paralle Adder and Subtacter.circ as structural Verilog: 1 circuit, main circuit main
module main (
  input  B3,
  input  A3,
  input  B2,
  input  A2,
  input  B1,
  input  A1,
  input  B0,
  input  A0,
  input  m,
  output Comanout_MSB,
  output S3,
  output S2,
  output S1,
  output S0
);

  wire adder_2_cout, adder_3_cout, adder_4_cout, xor_1_out, xor_2_out, xor_3_out, xor_4_out;

  xor xor_1 (xor_1_out, m, B3);
  Adder #(.width(1)) adder_1 (.a(A3), .b(xor_1_out), .out(S3), .cin(adder_2_cout), .cout(Comanout_MSB));
  xor xor_2 (xor_2_out, m, B2);
  Adder #(.width(1)) adder_2 (.a(A2), .b(xor_2_out), .out(S2), .cin(adder_3_cout), .cout(adder_2_cout));
  xor xor_3 (xor_3_out, m, B1);
  Adder #(.width(1)) adder_3 (.a(A1), .b(xor_3_out), .out(S1), .cin(adder_4_cout), .cout(adder_3_cout));
  xor xor_4 (xor_4_out, m, B0);
  Adder #(.width(1)) adder_4 (.a(A0), .b(xor_4_out), .out(S0), .cin(m), .cout(adder_4_cout));

  // Notes on the sheet:
  //   Dwij desai
  //   BDA08
  //   Batch-14
  //   Parealle
  //   Adder and subtacter
  //   subracter as adder
endmodule
